// Logisim project 2 BIT BINARY COUNTER.circ as structural Verilog: 1 circuit, main circuit main
module main (
  input  in_1,
  input  in_2
);

  wire clock_1_out, j_k_ff_1_q, j_k_ff_1_qn, j_k_ff_2_q;

  Clock clock_1 (.out(clock_1_out));
  J_K_Flip_Flop j_k_ff_1 (
    .J(in_2), .clk(clock_1_out), .K(in_2), .Q(j_k_ff_1_q), .Qn(j_k_ff_1_qn));  // open: preset, en, reset
  J_K_Flip_Flop j_k_ff_2 (
    .J(j_k_ff_1_qn), .clk(j_k_ff_1_qn), .K(j_k_ff_1_qn), .Q(j_k_ff_2_q));  // open: Qn, preset, en, reset
  LED Q1 (.in(j_k_ff_2_q));
  LED Q0 (.in(j_k_ff_1_q));
endmodule
