// Logisim project 3 BIT SYNCHRONOUS.circ as structural Verilog: 1 circuit, main circuit main
module main (
  input  COUNT_ENABLE
);

  wire and_1_out, and_2_out, and_3_out, clock_1_out, j_k_ff_1_q, j_k_ff_2_q, j_k_ff_3_q;

  Clock clock_1 (.out(clock_1_out));
  and and_1 (and_1_out, COUNT_ENABLE, j_k_ff_1_q);
  and and_2 (and_2_out, and_1_out, j_k_ff_2_q);
  J_K_Flip_Flop j_k_ff_1 (
    .J(COUNT_ENABLE), .clk(clock_1_out), .K(COUNT_ENABLE), .Q(j_k_ff_1_q));  // open: Qn, preset, en, reset
  J_K_Flip_Flop j_k_ff_2 (
    .J(and_1_out), .clk(clock_1_out), .K(and_1_out), .Q(j_k_ff_2_q));  // open: Qn, preset, en, reset
  J_K_Flip_Flop j_k_ff_3 (
    .J(and_2_out), .clk(clock_1_out), .K(and_2_out), .Q(j_k_ff_3_q));  // open: Qn, preset, en, reset
  and and_3 (and_3_out, j_k_ff_3_q, and_2_out);
  LED A0 (.in(j_k_ff_1_q));
  LED A1 (.in(j_k_ff_2_q));
  LED A2 (.in(j_k_ff_3_q));
  LED OUTPUT_CARRY (.in(and_3_out));
endmodule
