// Logisim project 4 BIT RIPPLE COUNTER.circ as structural Verilog: 1 circuit, main circuit main
module main (
  input  in_1,
  input  in_2
);

  wire clock_1_out, clock_2_out, j_k_ff_1_q, j_k_ff_2_q, j_k_ff_3_q, j_k_ff_4_q, j_k_ff_5_q, j_k_ff_6_q,
       j_k_ff_7_q, j_k_ff_8_q;

  Clock clock_1 (.out(clock_1_out));
  Clock clock_2 (.out(clock_2_out));
  J_K_Flip_Flop j_k_ff_1 (.J(in_1), .clk(clock_1_out), .K(in_1), .Q(j_k_ff_1_q));  // open: Qn, preset, en, reset
  LED Q0 (.in(j_k_ff_1_q));
  LED Q0_2 (.in(j_k_ff_2_q));
  J_K_Flip_Flop j_k_ff_2 (.J(in_2), .clk(clock_2_out), .K(in_2), .Q(j_k_ff_2_q));  // open: Qn, preset, en, reset
  LED Q1 (.in(j_k_ff_3_q));
  J_K_Flip_Flop j_k_ff_3 (.J(in_1), .clk(j_k_ff_1_q), .K(in_1), .Q(j_k_ff_3_q));  // open: Qn, preset, en, reset
  J_K_Flip_Flop j_k_ff_4 (.J(in_1), .clk(j_k_ff_3_q), .K(in_1), .Q(j_k_ff_4_q));  // open: Qn, preset, en, reset
  LED Q1_2 (.in(j_k_ff_5_q));
  J_K_Flip_Flop j_k_ff_5 (
    .J(j_k_ff_2_q), .clk(j_k_ff_2_q), .K(j_k_ff_2_q), .Q(j_k_ff_5_q));  // open: Qn, preset, en, reset
  LED Q2 (.in(j_k_ff_4_q));
  LED Q2_2 (.in(j_k_ff_6_q));
  J_K_Flip_Flop j_k_ff_6 (
    .J(j_k_ff_5_q), .clk(j_k_ff_5_q), .K(j_k_ff_5_q), .Q(j_k_ff_6_q));  // open: Qn, preset, en, reset
  LED Q3 (.in(j_k_ff_7_q));
  J_K_Flip_Flop j_k_ff_7 (.J(in_1), .clk(j_k_ff_4_q), .K(in_1), .Q(j_k_ff_7_q));  // open: Qn, preset, en, reset
  LED Q3_2 (.in(j_k_ff_8_q));
  J_K_Flip_Flop j_k_ff_8 (
    .J(j_k_ff_6_q), .clk(j_k_ff_6_q), .K(j_k_ff_6_q), .Q(j_k_ff_8_q));  // open: Qn, preset, en, reset

  // Notes on the sheet:
  //   4 BIT RIPPLE COUNTER
endmodule
