// Logisim project D FLIP FLOP.circ as structural Verilog: 1 circuit, main circuit main
module main (
  input  R
);

  wire clock_1_out, nand_1_out, nand_2_out, nand_3_out, nand_4_out, not_1_out;

  not not_1 (not_1_out, R);
  Clock clock_1 (.out(clock_1_out));
  nand nand_1 (nand_1_out, not_1_out, clock_1_out);
  nand nand_2 (nand_2_out, clock_1_out, R);
  nand nand_3 (nand_3_out, nand_1_out, nand_4_out);
  nand nand_4 (nand_4_out, nand_3_out, nand_2_out);
  LED Q (.in(nand_3_out));
  LED Q_prime (.in(nand_4_out));

  // Notes on the sheet:
  //   CLK
  //   D FLIP FLOP
endmodule
