// Logisim project DECADE COUNTER.circ as structural Verilog: 1 circuit, main circuit main
module main (
  input  in_1
);

  wire and_1_out, clock_1_out, j_k_ff_1_q, j_k_ff_2_q, j_k_ff_3_q, j_k_ff_4_q;

  Clock clock_1 (.out(clock_1_out));
  J_K_Flip_Flop #(.trigger("falling")) j_k_ff_1 (
    .J(in_1), .clk(clock_1_out), .K(in_1), .Q(j_k_ff_1_q), .reset(and_1_out));  // open: Qn, preset, en
  J_K_Flip_Flop #(.trigger("falling")) j_k_ff_2 (
    .J(in_1), .clk(j_k_ff_1_q), .K(in_1), .Q(j_k_ff_2_q), .reset(and_1_out));  // open: Qn, preset, en
  LED _8 (.in(j_k_ff_4_q));
  and and_1 (and_1_out, j_k_ff_4_q, j_k_ff_2_q);
  LED _4 (.in(j_k_ff_3_q));
  J_K_Flip_Flop #(.trigger("falling")) j_k_ff_3 (
    .J(in_1), .clk(j_k_ff_2_q), .K(in_1), .Q(j_k_ff_3_q), .reset(and_1_out));  // open: Qn, preset, en
  LED _1 (.in(j_k_ff_1_q));
  LED _2 (.in(j_k_ff_2_q));
  J_K_Flip_Flop #(.trigger("falling")) j_k_ff_4 (
    .J(in_1), .clk(j_k_ff_3_q), .K(in_1), .Q(j_k_ff_4_q), .reset(and_1_out));  // open: Qn, preset, en
endmodule
