// Logisim project J K FLIP FLOP.circ as structural Verilog: 1 circuit, main circuit main
module main (
  input  J,
  input  K
);

  wire clock_1_out, nand_1_out, nand_2_out, nand_3_out, nand_4_out;

  Clock clock_1 (.out(clock_1_out));
  nand nand_1 (nand_1_out, J, nand_4_out, clock_1_out);
  nand nand_2 (nand_2_out, clock_1_out, nand_3_out, K);
  nand nand_3 (nand_3_out, nand_1_out, nand_4_out);
  nand nand_4 (nand_4_out, nand_3_out, nand_2_out);
  LED Q (.in(nand_3_out));
  LED Q_prime (.in(nand_4_out));

  // Notes on the sheet:
  //   J K FLIP FLOP
endmodule
